# Fritzing sketch BME280_to_Nokia5110 (saved by Fritzing 0.9.3b)
breadboards: 1

parts:
  Nokia_5110_LCD_Module1 = Nokia 5110 LCD basado en PCD8544  # not connected
  Part1 = Arduino Nano (Rev3.0)
  Part2 = Adafruit BME280
  S1 = Momentary Switch [package=ksa_sealed_tac_switch]
  S2 = Momentary Switch [package=ksa_sealed_tac_switch]

nets:
  GND: Part1.GND, Part2.GND, S1.2, S2.2
  N1: Part1.D11/MOSI, S1.3
  N2: Part1.D12/MISO, S2.3
  N3: Part1.A5, Part2.SDO/ADR
  N4: Part1.A4, Part2.SCK/SCL
  3V3: Part1.3V3, Part2.VIN

custom parts:
  Nokia 5110 LCD basado en PCD8544: Módulo Nokia 5110 LCD basado en el controlador PCD8544. Versión de 8 pines (sólo entrada).
  Adafruit BME280: Bosch has stepped up their game with their new BME280 sensor, an environmental sensor with temperature, barometric pressure and humidity! This sensor is great for all sorts of weather/environmental sensing and can even be used in both I2C and SPI! This precision sensor from Bosch is the best low-cost sensing solution for measuring humidity with ±3% accuracy, barometric pressure with ±1 hPa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
